# Fritzing sketch LCDtext (saved by Fritzing 0.9.4)
breadboards: 1

parts:
  Parça1 = Arduino Nano 33 BLE Sense
  Parça2 = LCD1602-I2C
  R1 = Resistor [tolerance=±5% resistance=220 package=THT]
  R2 = Resistor [tolerance=±5% resistance=220 package=THT]
  LED1 = LED - 5mm [color="Red (633nm)" package="5 mm [THT]"]
  LED2 = LED - 5mm [color="Green (555nm)" package="5 mm [THT]"]

nets:
  GND: Parça1.GND, Parça1.A7, Parça2.GND, LED1.cathode, LED2.cathode
  N1: Parça1.D2, R1.Pin_0
  N2: Parça1.D3~, R2.Pin_0
  N3: Parça1.D11/MOSI, Parça1.+5V
  VIN: Parça1.VIN, Parça2.VCC
  N4: Parça1.A5, Parça2.SCL
  N5: Parça1.A4, Parça2.SDA
  N6: R1.Pin_1, LED2.anode
  N7: R2.Pin_1, LED1.anode

custom parts:
  Arduino Nano 33 BLE Sense: The Nano 33 BLE Sense (without headers) is Arduino’s 3.3V AI enabled board in the smallest available form factor: 45x18mm! The Arduino Nano 33 BLE Sense is a completely new board on a well-known form factor. It comes with a series of embedded sensors: 9 axis inertial sensor: what makes this board ideal for wearable devices humidity, and temperature sensor: to get highly accurate measurements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
  LCD1602-I2C: A standard character display, usually with 2x16 characters. Comes in many colors with LCM1602 IIC attached.
